// Logisim project BobbyKingDigitalDesignLab5.circ as structural Verilog: 1 circuit, main circuit main
module main (
  input  x,
  input  y,
  input  cin,
  output z,
  output cout
);

  wire and_1_out, and_2_out, and_3_out, and_4_out, and_5_out, and_6_out, and_7_out, not_1_out, not_2_out,
       not_3_out;

  not not_1 (not_1_out, x);
  not not_2 (not_2_out, y);
  not not_3 (not_3_out, cin);
  and and_1 (and_1_out, not_1_out, not_2_out, cin);
  and and_2 (and_2_out, not_1_out, y, not_3_out);
  and and_3 (and_3_out, x, not_2_out, not_3_out);
  and and_4 (and_4_out, x, y, cin);
  and and_5 (and_5_out, y, cin);
  and and_6 (and_6_out, x, cin);
  and and_7 (and_7_out, x, y);
  or or_1 (z, and_1_out, and_2_out, and_3_out, and_4_out);
  or or_2 (cout, and_5_out, and_6_out, and_7_out);

  // Notes on the sheet:
  //   FULL ADDER
endmodule
