// Logisim project Bobby_King_Lab_8.circ as structural Verilog: 1 circuit, main circuit main
module main (
  input  Input_1,
  input  Input_2,
  input  Input_3,
  output Output_1,
  output Output_2,
  output Output_4,
  output Output_3
);

  wire clk, decoder_1_out0, decoder_1_out1, decoder_1_out2, G_1, G_2, R_1, R_2;
  wire [1:0] counter_1_q, counter_2_q;

  Clock clock_1 (.out(clk));
  Decoder #(.select(2)) decoder_1 (
    .out0(decoder_1_out0), .out1(decoder_1_out1), .out2(decoder_1_out2), .out3(Output_4),
    .sel({Input_3, Input_2}), .en(Input_1));
  Counter #(.max('h3), .width(2)) counter_1 (
    .count(decoder_1_out1), .Q(counter_1_q), .clk(clk), .clr(decoder_1_out0));  // open: load, D, carry, up
  Counter #(.max('h3), .width(2)) counter_2 (
    .count(decoder_1_out2), .Q(counter_2_q), .clk(clk), .clr(decoder_1_out1));  // open: load, D, carry, up
  Counter #(.max('h7), .width(3)) counter_3 (
    .count(decoder_1_out0), .Q({Output_3, G_1, R_1}), .clk(clk));  // open: load, D, carry, up, clr
  or or_1 (R_2, counter_1_q[0], counter_1_q[1]);
  and and_1 (G_2, counter_2_q[0], counter_2_q[1]);
  or or_2 (Output_1, R_1, R_2);
  or or_3 (Output_2, G_1, G_2);

  // Other names for the same wires on the sheet: B = Output_3
endmodule
